// Logisim project 74Logic.circ as structural Verilog: 20 circuits, main circuit SN74LS01
module SN74LS01 (
  input  A1,
  input  B1,
  input  A2,
  input  B2,
  input  A3,
  input  B3,
  input  A4,
  input  B4,
  output Y1,
  output Y2,
  output Y3,
  output Y4
);

  wire and_1_out, and_2_out, and_3_out, and_4_out;

  and and_1 (and_1_out, A1, B1);
  and and_2 (and_2_out, A2, B2);
  and and_3 (and_3_out, A3, B3);
  and and_4 (and_4_out, A4, B4);
  assign Y1 = and_1_out ? 1'b0 : 1'bz;  // Controlled_Buffer controlled_buffer_1
  assign Y2 = and_2_out ? 1'b0 : 1'bz;  // Controlled_Buffer controlled_buffer_2
  assign Y3 = and_3_out ? 1'b0 : 1'bz;  // Controlled_Buffer controlled_buffer_3
  assign Y4 = and_4_out ? 1'b0 : 1'bz;  // Controlled_Buffer controlled_buffer_4
endmodule

module SN74LS03 (
  input  A1,
  input  B1,
  input  A2,
  input  B2,
  input  A3,
  input  B3,
  input  A4,
  input  B4,
  output Y1,
  output Y2,
  output Y3,
  output Y4
);

  wire and_1_out, and_2_out, and_3_out, and_4_out;

  and and_1 (and_1_out, A1, B1);
  and and_2 (and_2_out, A2, B2);
  and and_3 (and_3_out, A3, B3);
  and and_4 (and_4_out, A4, B4);
  assign Y1 = and_1_out ? 1'b0 : 1'bz;  // Controlled_Buffer controlled_buffer_1
  assign Y2 = and_2_out ? 1'b0 : 1'bz;  // Controlled_Buffer controlled_buffer_2
  assign Y3 = and_3_out ? 1'b0 : 1'bz;  // Controlled_Buffer controlled_buffer_3
  assign Y4 = and_4_out ? 1'b0 : 1'bz;  // Controlled_Buffer controlled_buffer_4
endmodule

module SN74LS05 (
  input  A1,
  input  A2,
  input  A3,
  input  A4,
  input  A5,
  input  A6,
  output Y1,
  output Y2,
  output Y3,
  output Y4,
  output Y5,
  output Y6
);

  assign Y1 = A1 ? 1'b0 : 1'bz;  // Controlled_Buffer controlled_buffer_1
  assign Y2 = A2 ? 1'b0 : 1'bz;  // Controlled_Buffer controlled_buffer_2
  assign Y3 = A3 ? 1'b0 : 1'bz;  // Controlled_Buffer controlled_buffer_3
  assign Y4 = A4 ? 1'b0 : 1'bz;  // Controlled_Buffer controlled_buffer_4
  assign Y5 = A5 ? 1'b0 : 1'bz;  // Controlled_Buffer controlled_buffer_5
  assign Y6 = A6 ? 1'b0 : 1'bz;  // Controlled_Buffer controlled_buffer_6
endmodule

module SN74LS06 (
  input  A1,
  input  A2,
  input  A3,
  input  A4,
  input  A5,
  input  A6,
  output Y1,
  output Y2,
  output Y3,
  output Y4,
  output Y5,
  output Y6
);

  assign Y1 = A1 ? 1'b0 : 1'bz;  // Controlled_Buffer controlled_buffer_1
  assign Y2 = A2 ? 1'b0 : 1'bz;  // Controlled_Buffer controlled_buffer_2
  assign Y3 = A3 ? 1'b0 : 1'bz;  // Controlled_Buffer controlled_buffer_3
  assign Y4 = A4 ? 1'b0 : 1'bz;  // Controlled_Buffer controlled_buffer_4
  assign Y5 = A5 ? 1'b0 : 1'bz;  // Controlled_Buffer controlled_buffer_5
  assign Y6 = A6 ? 1'b0 : 1'bz;  // Controlled_Buffer controlled_buffer_6
endmodule

module SN74LS07 (
  input  A1,
  input  A2,
  input  A3,
  input  A4,
  input  A5,
  input  A6,
  output Y1,
  output Y2,
  output Y3,
  output Y4,
  output Y5,
  output Y6
);

  wire not_1_out, not_2_out, not_3_out, not_4_out, not_5_out, not_6_out;

  assign Y1 = not_1_out ? 1'b0 : 1'bz;  // Controlled_Buffer controlled_buffer_1
  not not_1 (not_1_out, A1);
  assign Y2 = not_2_out ? 1'b0 : 1'bz;  // Controlled_Buffer controlled_buffer_2
  not not_2 (not_2_out, A2);
  assign Y3 = not_3_out ? 1'b0 : 1'bz;  // Controlled_Buffer controlled_buffer_3
  not not_3 (not_3_out, A3);
  assign Y4 = not_4_out ? 1'b0 : 1'bz;  // Controlled_Buffer controlled_buffer_4
  not not_4 (not_4_out, A4);
  assign Y5 = not_5_out ? 1'b0 : 1'bz;  // Controlled_Buffer controlled_buffer_5
  not not_5 (not_5_out, A5);
  assign Y6 = not_6_out ? 1'b0 : 1'bz;  // Controlled_Buffer controlled_buffer_6
  not not_6 (not_6_out, A6);
endmodule

module SN74LS09 (
  input  A1,
  input  B1,
  input  A2,
  input  B2,
  input  A3,
  input  B3,
  input  A4,
  input  B4,
  output Y1,
  output Y2,
  output Y3,
  output Y4
);

  wire nand_1_out, nand_2_out, nand_3_out, nand_4_out;

  nand nand_1 (nand_1_out, A1, B1);
  nand nand_2 (nand_2_out, A2, B2);
  nand nand_3 (nand_3_out, A3, B3);
  nand nand_4 (nand_4_out, A4, B4);
  assign Y1 = nand_1_out ? 1'b0 : 1'bz;  // Controlled_Buffer controlled_buffer_1
  assign Y2 = nand_2_out ? 1'b0 : 1'bz;  // Controlled_Buffer controlled_buffer_2
  assign Y3 = nand_3_out ? 1'b0 : 1'bz;  // Controlled_Buffer controlled_buffer_3
  assign Y4 = nand_4_out ? 1'b0 : 1'bz;  // Controlled_Buffer controlled_buffer_4
endmodule

module SN74LS12 (
  input  A1,
  input  B1,
  input  C1,
  input  A2,
  input  B2,
  input  C2,
  input  A3,
  input  B3,
  input  C3,
  output Y1,
  output Y2,
  output Y3
);

  wire and_1_out, and_2_out, and_3_out;

  and and_1 (and_1_out, A1, B1, C1);
  and and_2 (and_2_out, A2, B2, C2);
  and and_3 (and_3_out, A3, B3, C3);
  assign Y1 = and_1_out ? 1'b0 : 1'bz;  // Controlled_Buffer controlled_buffer_1
  assign Y2 = and_2_out ? 1'b0 : 1'bz;  // Controlled_Buffer controlled_buffer_2
  assign Y3 = and_3_out ? 1'b0 : 1'bz;  // Controlled_Buffer controlled_buffer_3
endmodule

module SN74LS15 (
  input  A1,
  input  B1,
  input  C1,
  input  A2,
  input  B2,
  input  C2,
  input  A3,
  input  B3,
  input  C3,
  output Y1,
  output Y2,
  output Y3
);

  wire nand_1_out, nand_2_out, nand_3_out;

  nand nand_1 (nand_1_out, A1, B1, C1);
  nand nand_2 (nand_2_out, A2, B2, C2);
  nand nand_3 (nand_3_out, A3, B3, C3);
  assign Y1 = nand_1_out ? 1'b0 : 1'bz;  // Controlled_Buffer controlled_buffer_1
  assign Y2 = nand_2_out ? 1'b0 : 1'bz;  // Controlled_Buffer controlled_buffer_2
  assign Y3 = nand_3_out ? 1'b0 : 1'bz;  // Controlled_Buffer controlled_buffer_3
endmodule

module SN74LS16 (
  input  A1,
  input  A2,
  input  A3,
  input  A4,
  input  A5,
  input  A6,
  output Y1,
  output Y2,
  output Y3,
  output Y4,
  output Y5,
  output Y6
);

  assign Y1 = A1 ? 1'b0 : 1'bz;  // Controlled_Buffer controlled_buffer_1
  assign Y2 = A2 ? 1'b0 : 1'bz;  // Controlled_Buffer controlled_buffer_2
  assign Y3 = A3 ? 1'b0 : 1'bz;  // Controlled_Buffer controlled_buffer_3
  assign Y4 = A4 ? 1'b0 : 1'bz;  // Controlled_Buffer controlled_buffer_4
  assign Y5 = A5 ? 1'b0 : 1'bz;  // Controlled_Buffer controlled_buffer_5
  assign Y6 = A6 ? 1'b0 : 1'bz;  // Controlled_Buffer controlled_buffer_6
endmodule

module SN74LS17 (
  input  A1,
  input  A2,
  input  A3,
  input  A4,
  input  A5,
  input  A6,
  output Y1,
  output Y2,
  output Y3,
  output Y4,
  output Y5,
  output Y6
);

  wire not_1_out, not_2_out, not_3_out, not_4_out, not_5_out, not_6_out;

  assign Y1 = not_1_out ? 1'b0 : 1'bz;  // Controlled_Buffer controlled_buffer_1
  not not_1 (not_1_out, A1);
  assign Y2 = not_2_out ? 1'b0 : 1'bz;  // Controlled_Buffer controlled_buffer_2
  not not_2 (not_2_out, A2);
  assign Y3 = not_3_out ? 1'b0 : 1'bz;  // Controlled_Buffer controlled_buffer_3
  not not_3 (not_3_out, A3);
  assign Y4 = not_4_out ? 1'b0 : 1'bz;  // Controlled_Buffer controlled_buffer_4
  not not_4 (not_4_out, A4);
  assign Y5 = not_5_out ? 1'b0 : 1'bz;  // Controlled_Buffer controlled_buffer_5
  not not_5 (not_5_out, A5);
  assign Y6 = not_6_out ? 1'b0 : 1'bz;  // Controlled_Buffer controlled_buffer_6
  not not_6 (not_6_out, A6);
endmodule

module SN74LS22 (
  input  A1,
  input  B1,
  input  C1,
  input  D1,
  input  A2,
  input  B2,
  input  C2,
  input  D2,
  output Y1,
  output Y2
);

  wire and_1_out, and_2_out;

  and and_1 (and_1_out, A1, B1, C1, D1);
  and and_2 (and_2_out, A2, B2, C2, D2);
  assign Y1 = and_1_out ? 1'b0 : 1'bz;  // Controlled_Buffer controlled_buffer_1
  assign Y2 = and_2_out ? 1'b0 : 1'bz;  // Controlled_Buffer controlled_buffer_2
endmodule

module SN74LS23 (
  input  A1,
  input  B1,
  input  C1,
  input  X1,
  input  D1,
  input  X1n,
  input  G1,
  input  A2,
  input  B2,
  input  C2,
  input  D2,
  input  G2,
  output Y1,
  output Y2
);

  wire and_1_out, and_2_out, and_3_out, and_4_out, and_5_out, and_6_out, and_7_out, and_8_out, and_9_out,
       not_1_out, or_1_out;

  and and_1 (and_1_out, A1, G1);
  and and_2 (and_2_out, B1, G1);
  and and_3 (and_3_out, C1, G1);
  and and_4 (and_4_out, D1, G1);
  and and_5 (and_5_out, A2, G2);
  and and_6 (and_6_out, B2, G2);
  and and_7 (and_7_out, C2, G2);
  and and_8 (and_8_out, D2, G2);
  not not_1 (not_1_out, X1n);
  or or_1 (or_1_out, and_1_out, and_2_out, and_3_out, and_4_out);
  assign Y1 = and_9_out ? or_1_out : 1'bz;  // Controlled_Buffer controlled_buffer_1
  and and_9 (and_9_out, X1, not_1_out);
  nor nor_1 (Y2, and_5_out, and_6_out, and_7_out, and_8_out);
endmodule

module SN74LS25 (
  input  A1,
  input  B1,
  input  C1,
  input  D1,
  input  G1,
  input  A2,
  input  B2,
  input  C2,
  input  D2,
  input  G2,
  output Y1,
  output Y2
);

  wire and_1_out, and_2_out, and_3_out, and_4_out, and_5_out, and_6_out, and_7_out, and_8_out;

  and and_1 (and_1_out, A1, G1);
  and and_2 (and_2_out, B1, G1);
  and and_3 (and_3_out, C1, G1);
  and and_4 (and_4_out, D1, G1);
  and and_5 (and_5_out, A2, G2);
  and and_6 (and_6_out, B2, G2);
  and and_7 (and_7_out, C2, G2);
  and and_8 (and_8_out, D2, G2);
  or or_1 (Y1, and_1_out, and_2_out, and_3_out, and_4_out);
  nor nor_1 (Y2, and_5_out, and_6_out, and_7_out, and_8_out);
endmodule

module SN74LS26 (
  input  A1,
  input  B1,
  input  A2,
  input  B2,
  input  A3,
  input  B3,
  input  A4,
  input  B4,
  output Y1,
  output Y2,
  output Y3,
  output Y4
);

  wire and_1_out, and_2_out, and_3_out, and_4_out;

  and and_1 (and_1_out, A1, B1);
  and and_2 (and_2_out, A2, B2);
  and and_3 (and_3_out, A3, B3);
  and and_4 (and_4_out, A4, B4);
  assign Y1 = and_1_out ? 1'b0 : 1'bz;  // Controlled_Buffer controlled_buffer_1
  assign Y2 = and_2_out ? 1'b0 : 1'bz;  // Controlled_Buffer controlled_buffer_2
  assign Y3 = and_3_out ? 1'b0 : 1'bz;  // Controlled_Buffer controlled_buffer_3
  assign Y4 = and_4_out ? 1'b0 : 1'bz;  // Controlled_Buffer controlled_buffer_4
endmodule

module SN74LS28 (
  input  A1,
  input  B1,
  input  A2,
  input  B2,
  input  A3,
  input  B3,
  input  A4,
  input  B4,
  output Y1,
  output Y2,
  output Y3,
  output Y4
);

  nor nor_1 (Y1, A1, B1);
  nor nor_2 (Y2, A2, B2);
  nor nor_3 (Y3, A3, B3);
  nor nor_4 (Y4, A4, B4);
endmodule

module SN74LS30 (
  input  A,
  input  B,
  input  C,
  input  D,
  input  E,
  input  F,
  input  G,
  input  H,
  output Y
);

  nand nand_1 (Y, A, B, C, D, E, F, G, H);
endmodule

module SN74LS33 (
  input  A1,
  input  B1,
  input  A2,
  input  B2,
  input  A3,
  input  B3,
  input  A4,
  input  B4,
  output Y1,
  output Y2,
  output Y3,
  output Y4
);

  wire or_1_out, or_2_out, or_3_out, or_4_out;

  or or_1 (or_1_out, A1, B1);
  or or_2 (or_2_out, A2, B2);
  or or_3 (or_3_out, A3, B3);
  or or_4 (or_4_out, A4, B4);
  assign Y1 = or_1_out ? 1'b0 : 1'bz;  // Controlled_Buffer controlled_buffer_1
  assign Y2 = or_2_out ? 1'b0 : 1'bz;  // Controlled_Buffer controlled_buffer_2
  assign Y3 = or_3_out ? 1'b0 : 1'bz;  // Controlled_Buffer controlled_buffer_3
  assign Y4 = or_4_out ? 1'b0 : 1'bz;  // Controlled_Buffer controlled_buffer_4
endmodule

module SN74LS38 (
  input  A1,
  input  B1,
  input  A2,
  input  B2,
  input  A3,
  input  B3,
  input  A4,
  input  B4,
  output Y1,
  output Y2,
  output Y3,
  output Y4
);

  wire and_1_out, and_2_out, and_3_out, and_4_out;

  and and_1 (and_1_out, A1, B1);
  and and_2 (and_2_out, A2, B2);
  and and_3 (and_3_out, A3, B3);
  and and_4 (and_4_out, A4, B4);
  assign Y1 = and_1_out ? 1'b0 : 1'bz;  // Controlled_Buffer controlled_buffer_1
  assign Y2 = and_2_out ? 1'b0 : 1'bz;  // Controlled_Buffer controlled_buffer_2
  assign Y3 = and_3_out ? 1'b0 : 1'bz;  // Controlled_Buffer controlled_buffer_3
  assign Y4 = and_4_out ? 1'b0 : 1'bz;  // Controlled_Buffer controlled_buffer_4
endmodule

module SN74LS373 (
  input  OC,
  input  D1,
  input  C,
  input  D2,
  input  D3,
  input  D4,
  input  D5,
  input  D6,
  input  D7,
  input  D8,
  output Q1,
  output Q2,
  output Q3,
  output Q4,
  output Q5,
  output Q6,
  output Q7,
  output Q8
);

  wire nand_1_out, nand_2_out, nand_3_out, nand_4_out, nand_5_out, nand_6_out, nand_7_out, nand_8_out,
       nand_9_out, nand_10_out, nand_11_out, nand_12_out, nand_13_out, nand_14_out, nand_15_out, nand_16_out,
       nand_17_out, nand_18_out, nand_19_out, nand_20_out, nand_21_out, nand_22_out, nand_23_out,
       nand_24_out, nand_25_out, nand_26_out, nand_27_out, nand_28_out, nand_29_out, nand_30_out,
       nand_31_out, nand_32_out, not_1_out, not_2_out, not_3_out, not_4_out, not_5_out, not_6_out, not_7_out,
       not_8_out, not_9_out;

  not not_1 (not_1_out, OC);
  not not_2 (not_2_out, D1);
  not not_3 (not_3_out, D2);
  not not_4 (not_4_out, D3);
  not not_5 (not_5_out, D4);
  not not_6 (not_6_out, D5);
  not not_7 (not_7_out, D6);
  not not_8 (not_8_out, D7);
  not not_9 (not_9_out, D8);
  nand nand_1 (nand_1_out, D1, C);
  nand nand_2 (nand_2_out, C, not_2_out);
  nand nand_3 (nand_3_out, D2, C);
  nand nand_4 (nand_4_out, C, not_3_out);
  nand nand_5 (nand_5_out, D3, C);
  nand nand_6 (nand_6_out, C, not_4_out);
  nand nand_7 (nand_7_out, D4, C);
  nand nand_8 (nand_8_out, C, not_5_out);
  nand nand_9 (nand_9_out, D5, C);
  nand nand_10 (nand_10_out, C, not_6_out);
  nand nand_11 (nand_11_out, D6, C);
  nand nand_12 (nand_12_out, C, not_7_out);
  nand nand_13 (nand_13_out, D7, C);
  nand nand_14 (nand_14_out, C, not_8_out);
  nand nand_15 (nand_15_out, D8, C);
  nand nand_16 (nand_16_out, C, not_9_out);
  nand nand_17 (nand_17_out, nand_1_out, nand_18_out);
  assign Q1 = not_1_out ? nand_17_out : 1'bz;  // Controlled_Buffer controlled_buffer_1
  nand nand_18 (nand_18_out, nand_17_out, nand_2_out);
  nand nand_19 (nand_19_out, nand_3_out, nand_20_out);
  assign Q2 = not_1_out ? nand_19_out : 1'bz;  // Controlled_Buffer controlled_buffer_2
  nand nand_20 (nand_20_out, nand_19_out, nand_4_out);
  nand nand_21 (nand_21_out, nand_5_out, nand_22_out);
  assign Q3 = not_1_out ? nand_21_out : 1'bz;  // Controlled_Buffer controlled_buffer_3
  nand nand_22 (nand_22_out, nand_21_out, nand_6_out);
  nand nand_23 (nand_23_out, nand_7_out, nand_24_out);
  assign Q4 = not_1_out ? nand_23_out : 1'bz;  // Controlled_Buffer controlled_buffer_4
  nand nand_24 (nand_24_out, nand_23_out, nand_8_out);
  nand nand_25 (nand_25_out, nand_9_out, nand_26_out);
  assign Q5 = not_1_out ? nand_25_out : 1'bz;  // Controlled_Buffer controlled_buffer_5
  nand nand_26 (nand_26_out, nand_25_out, nand_10_out);
  nand nand_27 (nand_27_out, nand_11_out, nand_28_out);
  assign Q6 = not_1_out ? nand_27_out : 1'bz;  // Controlled_Buffer controlled_buffer_6
  nand nand_28 (nand_28_out, nand_27_out, nand_12_out);
  nand nand_29 (nand_29_out, nand_13_out, nand_30_out);
  assign Q7 = not_1_out ? nand_29_out : 1'bz;  // Controlled_Buffer controlled_buffer_7
  nand nand_30 (nand_30_out, nand_29_out, nand_14_out);
  nand nand_31 (nand_31_out, nand_15_out, nand_32_out);
  assign Q8 = not_1_out ? nand_31_out : 1'bz;  // Controlled_Buffer controlled_buffer_8
  nand nand_32 (nand_32_out, nand_31_out, nand_16_out);
endmodule

module SN74LS393 (
  input  A1,
  input  A2,
  input  CLR1,
  input  CLR2,
  output Q1A,
  output Q2A,
  output Q1B,
  output Q2B,
  output Q1C,
  output Q2C,
  output Q1D,
  output Q2D
);

  wire not_1_out, not_2_out, t_ff_1_qn, t_ff_2_qn, t_ff_3_qn, t_ff_5_qn, t_ff_6_qn, t_ff_7_qn;

  not not_1 (not_1_out, A1);
  T_Flip_Flop t_ff_1 (.T(1'b1), .clk(not_1_out), .Q(Q1A), .Qn(t_ff_1_qn), .reset(CLR1));  // open: preset
  T_Flip_Flop t_ff_2 (.T(1'b1), .clk(t_ff_1_qn), .Q(Q1B), .Qn(t_ff_2_qn), .reset(CLR1));  // open: preset
  T_Flip_Flop t_ff_3 (.T(1'b1), .clk(t_ff_2_qn), .Q(Q1C), .Qn(t_ff_3_qn), .reset(CLR1));  // open: preset
  T_Flip_Flop t_ff_4 (.T(1'b1), .clk(t_ff_3_qn), .Q(Q1D), .reset(CLR1));  // open: Qn, preset
  not not_2 (not_2_out, A2);
  T_Flip_Flop t_ff_5 (.T(1'b1), .clk(not_2_out), .Q(Q2A), .Qn(t_ff_5_qn), .reset(CLR2));  // open: preset
  T_Flip_Flop t_ff_6 (.T(1'b1), .clk(t_ff_5_qn), .Q(Q2B), .Qn(t_ff_6_qn), .reset(CLR2));  // open: preset
  T_Flip_Flop t_ff_7 (.T(1'b1), .clk(t_ff_6_qn), .Q(Q2C), .Qn(t_ff_7_qn), .reset(CLR2));  // open: preset
  T_Flip_Flop t_ff_8 (.T(1'b1), .clk(t_ff_7_qn), .Q(Q2D), .reset(CLR2));  // open: Qn, preset
endmodule
