// Logisim project FairchildDM81.circ as structural Verilog: 3 circuits, main circuit DM81LS95A
module DM81LS95A (
  input  A1,
  input  A2,
  input  A3,
  input  G1,
  input  A4,
  input  G2,
  input  A5,
  input  A6,
  input  A7,
  input  A8,
  output Y1,
  output Y2,
  output Y3,
  output Y4,
  output Y5,
  output Y6,
  output Y7,
  output Y8
);

  wire nor_1_out;

  nor nor_1 (nor_1_out, G1, G2);
  assign Y1 = nor_1_out ? A1 : 1'bz;  // Controlled_Buffer controlled_buffer_1
  assign Y2 = nor_1_out ? A2 : 1'bz;  // Controlled_Buffer controlled_buffer_2
  assign Y3 = nor_1_out ? A3 : 1'bz;  // Controlled_Buffer controlled_buffer_3
  assign Y4 = nor_1_out ? A4 : 1'bz;  // Controlled_Buffer controlled_buffer_4
  assign Y5 = nor_1_out ? A5 : 1'bz;  // Controlled_Buffer controlled_buffer_5
  assign Y6 = nor_1_out ? A6 : 1'bz;  // Controlled_Buffer controlled_buffer_6
  assign Y7 = nor_1_out ? A7 : 1'bz;  // Controlled_Buffer controlled_buffer_7
  assign Y8 = nor_1_out ? A8 : 1'bz;  // Controlled_Buffer controlled_buffer_8
endmodule

module DM81LS96A (
  input  A1,
  input  A2,
  input  A3,
  input  G1,
  input  A4,
  input  G2,
  input  A5,
  input  A6,
  input  A7,
  input  A8,
  output Y1,
  output Y2,
  output Y3,
  output Y4,
  output Y5,
  output Y6,
  output Y7,
  output Y8
);

  wire nor_1_out;

  nor nor_1 (nor_1_out, G1, G2);
  assign Y1 = nor_1_out ? ~A1 : 1'bz;  // Controlled_Inverter controlled_inverter_1
  assign Y2 = nor_1_out ? ~A2 : 1'bz;  // Controlled_Inverter controlled_inverter_2
  assign Y3 = nor_1_out ? ~A3 : 1'bz;  // Controlled_Inverter controlled_inverter_3
  assign Y4 = nor_1_out ? ~A4 : 1'bz;  // Controlled_Inverter controlled_inverter_4
  assign Y5 = nor_1_out ? ~A5 : 1'bz;  // Controlled_Inverter controlled_inverter_5
  assign Y6 = nor_1_out ? ~A6 : 1'bz;  // Controlled_Inverter controlled_inverter_6
  assign Y7 = nor_1_out ? ~A7 : 1'bz;  // Controlled_Inverter controlled_inverter_7
  assign Y8 = nor_1_out ? ~A8 : 1'bz;  // Controlled_Inverter controlled_inverter_8
endmodule

module DM81LS97A (
  input  A1,
  input  A2,
  input  A3,
  input  A4,
  input  G1,
  input  A5,
  input  G2,
  input  A6,
  input  A7,
  input  A8,
  output Y1,
  output Y2,
  output Y3,
  output Y4,
  output Y5,
  output Y6,
  output Y7,
  output Y8
);

  wire not_1_out, not_2_out;

  not not_1 (not_1_out, G1);
  not not_2 (not_2_out, G2);
  assign Y1 = not_1_out ? A1 : 1'bz;  // Controlled_Buffer controlled_buffer_1
  assign Y2 = not_1_out ? A2 : 1'bz;  // Controlled_Buffer controlled_buffer_2
  assign Y3 = not_1_out ? A3 : 1'bz;  // Controlled_Buffer controlled_buffer_3
  assign Y4 = not_1_out ? A4 : 1'bz;  // Controlled_Buffer controlled_buffer_4
  assign Y5 = not_2_out ? A5 : 1'bz;  // Controlled_Buffer controlled_buffer_5
  assign Y6 = not_2_out ? A6 : 1'bz;  // Controlled_Buffer controlled_buffer_6
  assign Y7 = not_2_out ? A7 : 1'bz;  // Controlled_Buffer controlled_buffer_7
  assign Y8 = not_2_out ? A8 : 1'bz;  // Controlled_Buffer controlled_buffer_8
endmodule
